# Fritzing sketch DacomDoor Esp32 v1a 17x36 (saved by Fritzing 0.9.4)
perfboards: 1

parts:
  U2 = LuaNode32 / ESP32 [part_number=ESP32S-PIN30]
  RDM3600_Power = female pin header, 3 pins [form="♀ (female)"]
  RDM3600_Serial = female pin header, 5 pins [form="♀ (female)"]
  RDM3600_Antenna = female pin header, 2 pins [form="♀ (female)"]
  Speaker = male pin header, 2 pins [form="♂ (male)"]
  LED_Status = male pin header, 2 pins [form="♂ (male)"]
  CmdBtn_ext = male pin header, 2 pins [form="♂ (male)"]
  LDR_or_Jumper = Photocell (LDR) [package=THT]  # not connected
  ReedSwitch = Reed switch [package=THT]  # not connected
  DoorOpenedSensor = male pin header, 2 pins [form="♂ (male)"]
  LDR = male pin header, 2 pins [form="♂ (male)"]
  Antenna = male pin header, 2 pins [form="♂ (male)"]
  Relay = OMRON PCB Power Relay – G5LE [part_number="G5LE-1\n" package=THT]
  ProgBtn = Pushbutton [package="[THT]"]
  Relay_Diode = Rectifier Diode [part_number=1N4001 package="300 mil [THT]"]
  R1 = Resistor [tolerance=±5% resistance=510 package=THT]
  U1 = TRANSISTOR_NPN_2 [part_number=327 package=to-92]
  OUTPUT = screw terminal, 2 pins
  NF_NA = female pin header, 3 pins [form="♀ (female)"]
  Vin_Protection_Diode = Rectifier Diode [part_number=1N4004 package="300 mil [THT]"]
  5V_in = female pin header, 2 pins [form="♀ (female)"]
  R5 = Resistor [tolerance=±5% resistance=10k package=THT]
  R6 = Resistor [tolerance=±5% resistance=510 package=THT]

nets:
  N1: U2.D13, R1.Pin_1
  N2: U2.GND, RDM3600_Power.pin3, Speaker.pin1, LED_Status.pin1, CmdBtn_ext.pin1, DoorOpenedSensor.pin2, LDR.pin2, ProgBtn.Pin_1, ProgBtn.Pin_2, U1.E, Vin_Protection_Diode.anode, 5V_in.pin2
  N3: U2.Vin, RDM3600_Power.pin2, Relay.COIL2, Relay_Diode.cathode, Vin_Protection_Diode.cathode, 5V_in.pin1, R5.Pin_1
  N4: U2.D15, LED_Status.pin2
  N5: U2.D2, R6.Pin_1
  N6: U2.D4, CmdBtn_ext.pin2
  N7: U2.TX2, DoorOpenedSensor.pin1
  N8: U2.D5, LDR.pin1, R5.Pin_0
  N9: U2.D18, ProgBtn.Pin_3
  N10: U2.RX0, RDM3600_Serial.pin1
  N11: RDM3600_Antenna.pin1, Antenna.pin1
  N12: RDM3600_Antenna.pin2, Antenna.pin2
  N13: Speaker.pin2, R6.Pin_0
  N14: Relay.A, NF_NA.pin3
  N15: Relay.COIL1, Relay_Diode.anode, U1.C
  N16: Relay.C, OUTPUT.pin1
  N17: Relay.B, NF_NA.pin1
  N18: R1.Pin_0, U1.B
  N19: OUTPUT.pin2, NF_NA.pin2

notes:
  12v and 5v sources
  RFid Antenna
  Action Button
  Speaker
  Led Status
  Output
  Prog Button
  5v in
  NF NA

custom parts:
  LuaNode32 / ESP32: New Image for LuaNode32 DOIT ESP32 DEVKIT V1. Base parts from LuaNode32 / ESP32 ESP32 based LuaNode32 by G.Noorlander DOIT Esp32 DevKit v1 (30 pins long, 11 pins width) by Werner Rothschopf (modified by vanepp Dec 2018)
