# Fritzing sketch DacomDoor Esp32 v1c stepdown 18x24 (saved by Fritzing 0.9.4)
perfboards: 1

parts:
  U2 = LuaNode32 / ESP32 [part_number=ESP32S-PIN30]  # not connected
  RDM3600_Power = female pin header, 3 pins [form="♀ (female)"]
  RDM3600_Serial = female pin header, 5 pins [form="♀ (female)"]
  RDM3600_Antenna = female pin header, 2 pins [form="♀ (female)"]
  Speaker = male pin header, 2 pins [form="♂ (male)"]
  LED_Status = male pin header, 2 pins [form="♂ (male)"]
  CmdBtn_ext = male pin header, 2 pins [form="♂ (male)"]
  LDR_or_Jumper = Photocell (LDR) [package=THT]  # not connected
  ReedSwitch = Reed switch [package=THT]  # not connected
  DoorOpenedSensor = male pin header, 2 pins [form="♂ (male)"]
  LDR = male pin header, 2 pins [form="♂ (male)"]
  Antenna = male pin header, 2 pins [form="♂ (male)"]
  Relay = OMRON PCB Power Relay – G5LE [part_number="G5LE-1\n" package=THT]
  ProgBtn = Pushbutton [package="[THT]"]
  Relay_Diode = Rectifier Diode [part_number=1N4001 package="300 mil [THT]"]
  R1 = Resistor [tolerance=±5% resistance=510 package=THT]
  U1 = TRANSISTOR_NPN_2 [part_number=327 package=to-92]
  NF_NA = female pin header, 3 pins [form="♀ (female)"]
  Vin_Protection_Diode = Rectifier Diode [part_number=1N4004 package="300 mil [THT]"]
  RDM3600_Serial1 = female pin header, 15 pins [form="♀ (female)"]
  RDM3600_Serial2 = female pin header, 15 pins [form="♀ (female)"]
  OUTPUT = screw terminal, 3 pins
  5V_in = female pin header, 3 pins [form="♀ (female)"]
  5V_in1 = female pin header, 3 pins [form="♀ (female)"]
  Power_plug1 = Power plug
  R2 = Resistor [tolerance=±5% resistance=0 package=THT]
  R3 = Resistor [tolerance=±5% resistance=510 package=THT]
  Relay_Diode2 = Rectifier Diode [part_number=1N4007 package="300 mil [THT]"]

nets:
  N1: RDM3600_Power.pin2, Relay.COIL1, Relay_Diode.cathode, Vin_Protection_Diode.cathode, RDM3600_Serial2.pin15, 5V_in.pin1
  N2: RDM3600_Power.pin3, Speaker.pin1, LED_Status.pin1, CmdBtn_ext.pin1, DoorOpenedSensor.pin2, LDR.pin2, ProgBtn.Pin_1, ProgBtn.Pin_2, Vin_Protection_Diode.anode, RDM3600_Serial1.pin14, 5V_in.pin3, 5V_in1.pin3
  N3: RDM3600_Serial.pin1, RDM3600_Serial1.pin4
  N4: RDM3600_Antenna.pin1, Antenna.pin1
  N5: RDM3600_Antenna.pin2, Antenna.pin2
  N6: Speaker.pin2, R3.Pin_0
  N7: LED_Status.pin2, RDM3600_Serial1.pin13
  N8: CmdBtn_ext.pin2, RDM3600_Serial1.pin11
  N9: DoorOpenedSensor.pin1, RDM3600_Serial1.pin9
  N10: LDR.pin1, RDM3600_Serial1.pin8
  N11: Relay.A, NF_NA.pin1
  N12: Relay.C, U1.E, RDM3600_Serial2.pin14, R2.Pin_1
  N13: Relay.COIL2, Relay_Diode.anode, U1.C
  N14: Relay.B, NF_NA.pin3
  N15: ProgBtn.Pin_3, ProgBtn.Pin_4, RDM3600_Serial1.pin7
  N16: R1.Pin_0, U1.B
  N17: R1.Pin_1, RDM3600_Serial2.pin13
  N18: NF_NA.pin2, OUTPUT.pin1, Relay_Diode2.anode
  N19: RDM3600_Serial1.pin12, R3.Pin_1
  N20: OUTPUT.pin3, 5V_in1.pin1, Power_plug1.VCC, Relay_Diode2.cathode

notes:
  12v stepdown to 5v
  RFid Antenna
  Action Button
  Speaker
  Led Status
  Output 12v
  Prog Button
  12v in
  NF NA
  5v out

custom parts:
  LuaNode32 / ESP32: New Image for LuaNode32 DOIT ESP32 DEVKIT V1. Base parts from LuaNode32 / ESP32 ESP32 based LuaNode32 by G.Noorlander DOIT Esp32 DevKit v1 (30 pins long, 11 pins width) by Werner Rothschopf (modified by vanepp Dec 2018)
