# Fritzing sketch DacomDoor Esp32C3 v2 18x24 DualSource (saved by Fritzing 0.9.4)
perfboards: 1

parts:
  RDM3600_Power = female pin header, 3 pins [form="♀ (female)"]
  RDM3600_Serial = female pin header, 5 pins [form="♀ (female)"]
  RDM3600_Antenna = female pin header, 2 pins [form="♀ (female)"]
  Speaker = male pin header, 2 pins [form="♂ (male)"]
  LED_Status = male pin header, 2 pins [form="♂ (male)"]
  CmdBtn_ext = male pin header, 2 pins [form="♂ (male)"]
  LDR_or_Jumper = Photocell (LDR) [package=THT]  # not connected
  ReedSwitch = Reed switch [package=THT]  # not connected
  DoorOpenedSensor = male pin header, 2 pins [form="♂ (male)"]
  LDR = male pin header, 2 pins [form="♂ (male)"]
  Antenna = male pin header, 2 pins [form="♂ (male)"]
  Relay = OMRON PCB Power Relay – G5LE [part_number="G5LE-1\n" package=THT]
  ProgBtn = Pushbutton [package="[THT]"]
  Relay_Diode = Rectifier Diode [part_number=1N4001 package="300 mil [THT]"]
  R1 = Resistor [tolerance=±5% resistance=510 package=THT]
  U1 = TRANSISTOR_NPN_2 [part_number=327 package=to-92]
  NF_NA = female pin header, 3 pins [form="♀ (female)"]
  Vin_Protection_Diode = Rectifier Diode [part_number=1N4004 package="300 mil [THT]"]
  R3 = Resistor [tolerance=±5% resistance=0 package=THT]
  OUTPUT = screw terminal, 3 pins
  RDM3600_Serial2 = female pin header, 8 pins [form="♀ (female)"]
  RDM3600_Serial1 = female pin header, 8 pins [form="♀ (female)"]
  5V_in = female pin header, 3 pins [form="♀ (female)"]
  R4 = Resistor [tolerance=±5% resistance=0 package=THT]
  R5 = Resistor [tolerance=±5% resistance=510 package=THT]

nets:
  N1: RDM3600_Power.pin1, Speaker.pin1, LED_Status.pin1, CmdBtn_ext.pin1, DoorOpenedSensor.pin2, LDR.pin2, ProgBtn.Pin_1, ProgBtn.Pin_2, U1.E, Vin_Protection_Diode.anode, RDM3600_Serial2.pin7, 5V_in.pin3
  N2: RDM3600_Serial.pin1, R3.Pin_0
  N3: RDM3600_Serial.pin5, Relay.COIL2, Relay_Diode.cathode, Vin_Protection_Diode.cathode, RDM3600_Serial2.pin8, R4.Pin_0
  N4: RDM3600_Antenna.pin1, Antenna.pin1
  N5: RDM3600_Antenna.pin2, Antenna.pin2
  N6: Speaker.pin2, R5.Pin_1
  N7: LED_Status.pin2, RDM3600_Serial2.pin1
  N8: CmdBtn_ext.pin2, RDM3600_Serial2.pin3
  N9: DoorOpenedSensor.pin1, RDM3600_Serial2.pin4
  N10: LDR.pin1, RDM3600_Serial2.pin5
  N11: Relay.A, NF_NA.pin3
  N12: Relay.COIL1, Relay_Diode.anode, U1.C
  N13: Relay.C, OUTPUT.pin1
  N14: Relay.B, NF_NA.pin1
  N15: ProgBtn.Pin_3, ProgBtn.Pin_4, RDM3600_Serial1.pin7
  N16: R1.Pin_0, U1.B
  N17: R1.Pin_1, RDM3600_Serial1.pin8
  N18: NF_NA.pin2, OUTPUT.pin3
  N19: R3.Pin_1, RDM3600_Serial1.pin2
  N20: RDM3600_Serial2.pin2, R5.Pin_0
  N21: 5V_in.pin2, R4.Pin_1

notes:
  12v and 5v sources
  RFid Antenna
  Action Button
  Speaker
  Led Status
  Output
  Prog Button
  5v in
  NF NA
