# Fritzing sketch DacomDoor v3 (saved by Fritzing 0.9.3b)
perfboards: 1

parts:
  R2 = Resistor [tolerance=±5% resistance=220 package="0603 [SMD]"]
  R9 = Resistor [tolerance=±5% resistance=510 package="0603 [SMD]"]
  RDM6300 = Header 6 [package=molex-1x6_lock]
  Antenna = Header 2 [package=molex-1x2_lock]
  LED_STATUS = Header 2 [package=molex-1x2_lock]
  U1 = TRANSISTOR_NPN_2 [package=to-92]
  NF_NA = Header 3 [package=molex-1x3_lock]
  D1 = Rectifier Diode [part_number=1N4001 package="Melf DO-213 AB [SMD]"]
  Emergency = Header 2 [package=molex-1x2_lock]
  OMRON1 = OMRON PCB Power Relay – G5LE [part_number="G5LE-1\n" package=THT]
  Antenna_Src = Header 2 [package=molex-1x2_lock]
  Program = Pushbutton [package="[SMD]"]
  CmdDoor = Pushbutton [package="[SMD]"]
  CmdDoor_con = Header 2 [package=molex-1x2_lock]
  Raspberry_Pi_1 = Raspberry Pi 3 [part_number=RPI-3-V1.2]

nets:
  N1: R2.Pin_0, Raspberry_Pi_1.GPIO23
  N2: R2.Pin_1, U1.B
  N3: R9.Pin_0, Raspberry_Pi_1.GPIO25
  N4: R9.Pin_1, LED_STATUS.1
  N5: RDM6300.1, D1.cathode, OMRON1.COIL2, Raspberry_Pi_1.5V
  N6: RDM6300.2, LED_STATUS.2, U1.E, Program.Pin_1, Program.Pin_2, CmdDoor.Pin_1, CmdDoor.Pin_2, CmdDoor_con.2, Raspberry_Pi_1.GND
  N7: RDM6300.5, Raspberry_Pi_1.GPIO15
  N8: Antenna.1, Antenna_Src.2
  N9: Antenna.2, Antenna_Src.1
  N10: U1.C, D1.anode, OMRON1.COIL1
  N11: NF_NA.1, Emergency.2
  N12: NF_NA.2, OMRON1.C
  N13: NF_NA.3, OMRON1.A
  N14: Emergency.1, OMRON1.B
  N15: Program.Pin_3, Program.Pin_4, Raspberry_Pi_1.GPIO16
  N16: CmdDoor.Pin_3, CmdDoor.Pin_4, CmdDoor_con.1, Raspberry_Pi_1.GPIO12
  3V3: Raspberry_Pi_1.3v3, Raspberry_Pi_1.3V3
