# Fritzing sketch DacomDoor v4 (saved by Fritzing 0.9.3b)
perfboards: 1

parts:
  R2 = Resistor [tolerance=±5% resistance=220 package="0603 [SMD]"]
  R9 = Resistor [tolerance=±5% resistance=510 package="0603 [SMD]"]
  Antenna = Header 2 [package=molex-1x2_lock]
  LED_STATUS = Header 2 [package=molex-1x2_lock]
  U1 = TRANSISTOR_NPN_2 [package=to-92]
  NF_NA = Header 3 [package=molex-1x3_lock]
  D1 = Rectifier Diode [part_number=1N4001 package="Melf DO-213 AB [SMD]"]
  Emergency = Header 2 [package=molex-1x2_lock]
  OMRON1 = OMRON PCB Power Relay – G5LE [part_number="G5LE-1\n" package=THT]
  Program = Pushbutton [package="[SMD]"]
  CmdDoor = Pushbutton [package="[SMD]"]
  CmdDoor_con = Header 2 [package=molex-1x2_lock]
  VCC = Header 1 [package=1x01_offset]
  RX = Header 1 [package=1x01_offset]  # not connected
  NC = Header 1 [package=1x01_offset]  # not connected
  GND = Header 1 [package=1x01_offset]
  TX = Header 1 [package=1x01_offset]
  Raspberry_Pi_1 = Raspberry Pi Zero
  Speaker = Header 2 [package=molex-1x2_lock]
  Antenna1 = Header 1 [package=1x01_offset]
  Antenna2 = Header 1 [package=1x01_offset]

nets:
  N1: R2.Pin_0, Raspberry_Pi_1.pin_16
  N2: R2.Pin_1, U1.B
  N3: R9.Pin_0, Raspberry_Pi_1.pin_18
  N4: R9.Pin_1, LED_STATUS.1
  N5: Antenna.1, Antenna2.1
  N6: Antenna.2, Antenna1.1
  N7: LED_STATUS.2, U1.E, Program.Pin_1, Program.Pin_2, CmdDoor.Pin_1, CmdDoor.Pin_2, CmdDoor_con.1, GND.1, Raspberry_Pi_1.pin_6, Raspberry_Pi_1.pin_20, Raspberry_Pi_1.pin_30, Speaker.2
  N8: U1.C, D1.anode, OMRON1.COIL2
  N9: NF_NA.1, OMRON1.B
  N10: NF_NA.2, OMRON1.C
  N11: NF_NA.3, Emergency.1
  N12: D1.cathode, OMRON1.COIL1, VCC.1, Raspberry_Pi_1.pin_2
  N13: Emergency.2, OMRON1.A
  N14: Program.Pin_3, Program.Pin_4, Raspberry_Pi_1.pin_36
  N15: CmdDoor.Pin_3, CmdDoor.Pin_4, CmdDoor_con.2, Raspberry_Pi_1.pin_22
  N16: TX.1, Raspberry_Pi_1.pin_10
  N17: Raspberry_Pi_1.pin_32, Speaker.1
