# Fritzing sketch DacomDoor v5 (saved by Fritzing 0.9.3b)
perfboards: 1

parts:
  R2 = Resistor [tolerance=±5% resistance=220 package="0603 [SMD]"]
  R9 = Resistor [tolerance=±5% resistance=510 package="0603 [SMD]"]
  Antenna = Header 2 [package=molex-1x2_lock]
  LED_STATUS = Header 2 [package=molex-1x2_lock]
  U1 = TRANSISTOR_NPN_2 [package=to-92]
  D1 = Rectifier Diode [part_number=1N4001 package="Melf DO-213 AB [SMD]"]
  OMRON1 = OMRON PCB Power Relay – G5LE [part_number="G5LE-1\n" package=THT]
  Program = Pushbutton [package="[SMD]"]
  CmdDoor = Pushbutton [package="[SMD]"]
  CmdDoor_con = Header 2 [package=molex-1x2_lock]
  VCC = Header 1 [package=1x01_offset]
  RX = Header 1 [package=1x01_offset]  # not connected
  NC = Header 1 [package=1x01_offset]  # not connected
  GND = Header 1 [package=1x01_offset]
  TX = Header 1 [package=1x01_offset]
  Raspberry_Pi_1 = Raspberry Pi Zero
  Speaker = Header 2 [package=molex-1x2_lock]
  Antenna1 = Header 1 [package=1x01_offset]
  Antenna2 = Header 1 [package=1x01_offset]
  C2 = Electrolytic Capacitor [capacitance=1000μF voltage=16V package="1010 [SMD, electrolytic]"]
  R10 = Resistor [tolerance=±5% resistance=22 package="0603 [SMD]"]
  JP1 = Header 10 [package=1x10-2mm-smd]
  JP2 = Header 10 [package=1x10-2mm-smd]
  NC1 = Header 1 [package=1x01_offset]  # not connected
  NC2 = Header 1 [package=1x01_offset]  # not connected
  NC3 = Header 1 [package=1x01_offset]  # not connected
  Doorlock = Header 2 [package=molex-1x2_lock]

nets:
  N1: R2.Pin_0, Raspberry_Pi_1.pin_18, JP1.9
  N2: R2.Pin_1, U1.B
  N3: R9.Pin_0, Raspberry_Pi_1.pin_16, JP1.8
  N4: R9.Pin_1, LED_STATUS.1
  N5: Antenna.1, Antenna2.1
  N6: Antenna.2, Antenna1.1
  N7: LED_STATUS.2, U1.E, GND.1, Raspberry_Pi_1.pin_6, Raspberry_Pi_1.pin_9, Raspberry_Pi_1.pin_14, Raspberry_Pi_1.pin_20, Speaker.2, C2.-, JP1.3, Doorlock.2
  N8: U1.C, D1.anode, OMRON1.COIL1
  N9: D1.cathode, OMRON1.COIL2, VCC.1, Raspberry_Pi_1.pin_2, Raspberry_Pi_1.pin_4, JP1.2
  N10: OMRON1.C, Doorlock.1
  N11: OMRON1.B, C2.+, R10.Pin_0
  N12: Program.Pin_1, Program.Pin_2, CmdDoor.Pin_1, CmdDoor.Pin_2, CmdDoor_con.1
  N13: Program.Pin_3, Program.Pin_4, Raspberry_Pi_1.pin_32, JP2.6
  N14: CmdDoor.Pin_3, CmdDoor.Pin_4, CmdDoor_con.2, Raspberry_Pi_1.pin_22, JP2.1
  N15: TX.1, Raspberry_Pi_1.pin_10, JP1.5
  N16: Raspberry_Pi_1.pin_12, Speaker.1, JP1.6
