# Fritzing sketch DacomDoor v6 (saved by Fritzing 0.9.3b)
circuit board: 8.46667cm x 5.64444cm
perfboards: 1

parts:
  R2 = Resistor [tolerance=±5% resistance=510 package="0603 [SMD]"]
  R9 = Resistor [tolerance=±5% resistance=510 package="0603 [SMD]"]
  U1 = TRANSISTOR_NPN_2 [package=to-92]
  D1 = Rectifier Diode [part_number=1N4001 package="Melf DO-213 AB [SMD]"]
  OMRON1 = OMRON PCB Power Relay – G5LE [part_number="G5LE-1\n" package=THT]
  CmdDoor_con = Header 2 [package=molex-1x2_lock]
  VCC = Header 1 [package=1x01_offset]
  RX = Header 1 [package=1x01_offset]  # not connected
  NC = Header 1 [package=1x01_offset]  # not connected
  GND = Header 1 [package=1x01_offset]
  TX = Header 1 [package=1x01_offset]
  Raspberry_Pi_1 = Raspberry Pi Zero
  Antenna1 = Header 1 [package=1x01_offset]
  Antenna2 = Header 1 [package=1x01_offset]
  C2 = Electrolytic Capacitor [capacitance=1000μF voltage=16V package="1010 [SMD, electrolytic]"]
  R10 = Resistor [tolerance=±5% resistance=22 package="0603 [SMD]"]
  GPIOa = Header 10 [package=1x10-2mm-smd]
  NC1 = Header 1 [package=1x01_offset]  # not connected
  NC2 = Header 1 [package=1x01_offset]  # not connected
  NC3 = Header 1 [package=1x01_offset]  # not connected
  Doorlock_12v = Header 2 [package=molex-1x2_lock]
  GPIOb = Header 10 [package=1x10-2mm-smd]
  5V_in = Header 1 [package=1x01_offset]
  GND_in = Header 1 [package=1x01_offset]
  12v_steped_up = Header 1 [package=1x01_offset]
  GND_out = Header 1 [package=1x01_offset]
  Antenna1_2 = Header 1 [package=1x01_offset]
  Antenna2_2 = Header 1 [package=1x01_offset]
  Led_Status_+ = Header 1 [package=1x01_offset]
  Led_Status_- = Header 1 [package=1x01_offset]
  Speaker_+ = Header 1 [package=1x01_offset]
  Speaker_- = Header 1 [package=1x01_offset]
  SW2 = DIP SWITCH [package=dipswitch-02]
  SW3 = DIP SWITCH [package=dipswitch-02]
  CmdEnable_+ = Header 1 [package=1x01_offset]
  CmdEnable_- = Header 1 [package=1x01_offset]
  R11 = Resistor [tolerance=±5% resistance=10k package="0603 [SMD]"]
  LDR_or_Jumper = Photocell (LDR) [package=THT]
  D2 = Rectifier Diode [part_number=1N4001 package="Melf DO-213 AB [SMD]"]

nets:
  N1: R2.Pin_0, Raspberry_Pi_1.pin_40, GPIOb.10
  N2: R2.Pin_1, U1.B
  N3: R9.Pin_0, Raspberry_Pi_1.pin_36, GPIOb.8
  N4: R9.Pin_1, Led_Status_+.1
  N5: U1.C, D1.anode, OMRON1.COIL1
  N6: U1.E, CmdDoor_con.2, GND.1, Raspberry_Pi_1.pin_6, Raspberry_Pi_1.pin_34, Raspberry_Pi_1.pin_39, C2.-, GPIOa.3, Doorlock_12v.2, GND_in.1, GND_out.1, Led_Status_-.1, Speaker_-.1, SW2.3, SW2.4, SW3.3, SW3.4, D2.anode
  N7: D1.cathode, OMRON1.COIL2, VCC.1, Raspberry_Pi_1.pin_2, Raspberry_Pi_1.pin_4, GPIOa.2, 5V_in.1
  N8: OMRON1.C, Doorlock_12v.1, D2.cathode
  N9: OMRON1.B, C2.+, R10.Pin_0
  N10: CmdDoor_con.1, CmdEnable_-.1, LDR_or_Jumper.pin_1
  N11: TX.1, Raspberry_Pi_1.pin_10, GPIOa.5
  N12: Raspberry_Pi_1.pin_12, GPIOa.6, SW2.2
  N13: Raspberry_Pi_1.pin_16, GPIOa.8, SW2.1, R11.Pin_1
  N14: Raspberry_Pi_1.pin_18, GPIOa.9, SW3.2
  N15: Raspberry_Pi_1.pin_22, GPIOb.1, SW3.1
  N16: Raspberry_Pi_1.pin_32, GPIOb.6, Speaker_+.1
  N17: Antenna1.1, Antenna1_2.1
  N18: Antenna2.1, Antenna2_2.1
  N19: R10.Pin_1, 12v_steped_up.1
  N20: CmdEnable_+.1, R11.Pin_0, LDR_or_Jumper.pin_0
