# Fritzing sketch DacomDoor v6a (saved by Fritzing 0.9.3b)
circuit board: 5cm x 10cm
perfboards: 1

parts:
  U1 = TRANSISTOR_NPN_2 [package=to-92]
  Relay = OMRON PCB Power Relay – G5LE [part_number="G5LE-1\n" package=THT]
  Raspberry_Pi_1 = Raspberry Pi Zero  # not connected
  LDR_or_Jumper = Photocell (LDR) [package=THT]
  ProgBtn = Pushbutton [package="[THT]"]
  ReedSwitch = Reed switch [package=THT]
  R12 = Resistor [tolerance=±5% resistance=10k package=THT]
  R9 = Resistor [tolerance=±5% resistance=510 package=THT]
  R2 = Resistor [tolerance=±5% resistance=510 package=THT]
  D1 = Rectifier Diode [part_number=1N4001 package="300 mil [THT]"]
  J5 = female pin header, 20 pins [form="♀ (female)"]
  RDM3600_Antenna = female pin header, 2 pins [form="♀ (female)"]
  RDM3600_Power = female pin header, 3 pins [form="♀ (female)"]
  NA12v-GND-NF12v = screw terminal, 3 pins
  RDM3600_Serial = female pin header, 5 pins [form="♀ (female)"]
  CmdBtn = Pushbutton [package="[THT]"]
  StepUp_In_- = female pin header, 1 pin [form="♀ (female)"]
  StepUp_In_+5v = female pin header, 1 pin [form="♀ (female)"]
  StepUp_Out_+12v = female pin header, 1 pin [form="♀ (female)"]
  StepUp_Out_- = female pin header, 1 pin [form="♀ (female)"]
  Speaker = male pin header, 2 pins [form="♂ (male)"]
  Antenna = male pin header, 2 pins [form="♂ (male)"]
  LED_Status = male pin header, 2 pins [form="♂ (male)"]
  CmdBtn_ext = male pin header, 2 pins [form="♂ (male)"]
  DoorOpenedSensor = male pin header, 2 pins [form="♂ (male)"]
  LDR = male pin header, 2 pins [form="♂ (male)"]
  R10 = Resistor [tolerance=±5% resistance=22 package=THT]
  C2 = Electrolytic Capacitor [capacitance=1000μF voltage=16V package="200 mil [THT, electrolytic]"]
  D2 = Rectifier Diode [part_number=1N4001 package="300 mil [THT]"]

nets:
  N1: U1.C, Relay.COIL1, D1.anode
  N2: U1.B, R2.Pin_1
  N3: U1.E, LDR_or_Jumper.pin_0, ProgBtn.Pin_3, ProgBtn.Pin_4, ReedSwitch.pin_1, J5.pin3, RDM3600_Power.pin3, NA12v-GND-NF12v.pin2, CmdBtn.Pin_3, CmdBtn.Pin_4, StepUp_In_-.pin1, StepUp_Out_-.pin1, Speaker.pin1, LED_Status.pin1, CmdBtn_ext.pin1, DoorOpenedSensor.pin2, LDR.pin2, D2.anode
  N4: Relay.A, NA12v-GND-NF12v.pin1, D2.cathode
  N5: Relay.C, R10.Pin_0, C2.+
  N6: Relay.COIL2, R12.Pin_1, D1.cathode, J5.pin1, J5.pin2, RDM3600_Power.pin2, StepUp_In_+5v.pin1
  N7: Relay.B, NA12v-GND-NF12v.pin3
  N8: LDR_or_Jumper.pin_1, R12.Pin_0, J5.pin9, LDR.pin1
  N9: ProgBtn.Pin_1, ProgBtn.Pin_2, J5.pin6
  N10: ReedSwitch.pin_2, J5.pin11, DoorOpenedSensor.pin1
  N11: R9.Pin_0, J5.pin18
  N12: R9.Pin_1, LED_Status.pin2
  N13: R2.Pin_0, J5.pin20
  N14: J5.pin5, RDM3600_Serial.pin1
  N15: J5.pin8, CmdBtn.Pin_1, CmdBtn.Pin_2, CmdBtn_ext.pin2
  N16: J5.pin16, Speaker.pin2
  N17: J5.pin17, C2.-
  N18: RDM3600_Antenna.pin1, Antenna.pin1
  N19: RDM3600_Antenna.pin2, Antenna.pin2
  N20: StepUp_Out_+12v.pin1, R10.Pin_1

notes:
  StepUp 5v-12v
