# Fritzing sketch DacomDoor v6c 18x24 (saved by Fritzing 0.9.4)
perfboards: 1

parts:
  U1 = TRANSISTOR_NPN_2 [part_number=327 package=to-92]
  Relay = OMRON PCB Power Relay – G5LE [part_number="G5LE-1\n" package=THT]
  Raspberry_Pi_1 = Raspberry Pi Zero  # not connected
  LDR_or_Jumper = Photocell (LDR) [package=THT]  # not connected
  ProgBtn = Pushbutton [package="[THT]"]
  ReedSwitch = Reed switch [package=THT]  # not connected
  R12 = Resistor [tolerance=±5% resistance=10k package=THT]
  R9 = Resistor [tolerance=±5% resistance=510 package=THT]
  R2 = Resistor [tolerance=±5% resistance=510 package=THT]
  D1 = Rectifier Diode [part_number=1N4001 package="300 mil [THT]"]
  J5 = female pin header, 20 pins [form="♀ (female)"]
  RDM3600_Power = female pin header, 3 pins [form="♀ (female)"]
  NA12v-GND-NF12v = screw terminal, 3 pins
  RDM3600_Serial = female pin header, 5 pins [form="♀ (female)"]
  Speaker = male pin header, 2 pins [form="♂ (male)"]
  Antenna = male pin header, 2 pins [form="♂ (male)"]
  LED_Status = male pin header, 2 pins [form="♂ (male)"]
  CmdBtn_ext = male pin header, 2 pins [form="♂ (male)"]
  DoorOpenedSensor = male pin header, 2 pins [form="♂ (male)"]
  LDR = male pin header, 2 pins [form="♂ (male)"]
  R13 = Resistor [tolerance=±5% resistance=10k package=THT]
  J6 = female pin header, 1 pin [form="♀ (female)"]
  J7 = female pin header, 1 pin [form="♀ (female)"]
  J8 = female pin header, 1 pin [form="♀ (female)"]
  J9 = female pin header, 2 pins [form="♀ (female)"]
  R14 = Resistor [tolerance=±5% resistance=10k package=THT]
  R15 = Resistor [tolerance=±5% resistance=10k package=THT]
  R16 = Resistor [tolerance=±5% resistance=0 package=THT]
  R17 = Resistor [tolerance=±5% resistance=0 package=THT]
  RDM3600_Antenna = female pin header, 2 pins [form="♀ (female)"]

nets (from the breadboard view):
  N1: U1.C, Relay.COIL1, D1.anode
  N2: U1.B, R2.Pin_1
  N3: U1.E, ProgBtn.Pin_3, ProgBtn.Pin_4, J5.pin3, J5.pin7, J5.pin10, J5.pin15, J5.pin17, RDM3600_Power.pin3, Speaker.pin1, LED_Status.pin1, CmdBtn_ext.pin1, DoorOpenedSensor.pin2, LDR.pin2, J6.pin1, J7.pin1, J8.pin1, J9.pin1
  N4: Relay.A, NA12v-GND-NF12v.pin3
  N5: Relay.C, NA12v-GND-NF12v.pin2
  N6: Relay.COIL2, D1.cathode, R16.Pin_0
  N7: Relay.B, NA12v-GND-NF12v.pin1
  N8: ProgBtn.Pin_1, ProgBtn.Pin_2, J5.pin6, R15.Pin_0
  N9: R12.Pin_0, J5.pin9, LDR.pin1
  N10: R12.Pin_1, J5.pin1, J5.pin2, RDM3600_Power.pin2, R13.Pin_1, J9.pin2, R14.Pin_1, R15.Pin_1, R16.Pin_1
  N11: R9.Pin_0, J5.pin18
  N12: R9.Pin_1, LED_Status.pin2
  N13: R2.Pin_0, J5.pin20
  N14: J5.pin5, RDM3600_Serial.pin1
  N15: J5.pin8, R14.Pin_0, R17.Pin_1
  N16: J5.pin11, DoorOpenedSensor.pin1, R13.Pin_0
  N17: J5.pin16, Speaker.pin2
  N18: Antenna.pin1, RDM3600_Antenna.pin1
  N19: Antenna.pin2, RDM3600_Antenna.pin2
  N20: CmdBtn_ext.pin2, R17.Pin_0

notes:
  12v and 5v sources
  RFid Antenna
  Led Status
  Speaker
  Action Button
  Prog Button
  5v in
  Output
  GPIO Pins  2     1
